// Logisim project opdracht 3.1.circ as structural Verilog: 1 circuit, main circuit main
module main (
  input  S1,
  input  S2,
  input  S3,
  input  S4
);

  wire and_1_out, not_1_out, not_2_out, or_1_out;

  not not_1 (not_1_out, S1);
  or or_1 (or_1_out, S3, S4);
  and and_1 (and_1_out, not_1_out, S2);
  LED L1 (.in(and_1_out));
  LED L2 (.in(not_2_out));
  not not_2 (not_2_out, or_1_out);
endmodule
