// Logisim project opdracht 3.4.circ as structural Verilog: 1 circuit, main circuit main
module main (
  input  S1,
  input  S2,
  input  S3,
  input  S5,
  input  S6,
  input  S7
);

  wire and_1_out, and_2_out, and_3_out, and_4_out, and_5_out, not_1_out, not_2_out, not_3_out, not_4_out,
       not_5_out, not_6_out, or_1_out, or_2_out, xor_1_out;

  not not_1 (not_1_out, S2);
  not not_2 (not_2_out, S1);
  not not_3 (not_3_out, S1);
  not not_4 (not_4_out, S3);
  not not_5 (not_5_out, S1);
  not not_6 (not_6_out, S2);
  and and_1 (and_1_out, S1, not_1_out, not_2_out);
  and and_2 (and_2_out, not_3_out, S2, not_4_out);
  and and_3 (and_3_out, not_5_out, not_6_out, S3);
  and and_4 (and_4_out, S1, S2, S3);
  ExactlyOne xor_1 (.out(xor_1_out), .in0(S5), .in2(S6), .in4(S7));
  and and_5 (and_5_out, S5, S6, S7);
  or or_1 (or_1_out, xor_1_out, and_5_out);
  LED L3 (.in(or_1_out));
  or or_2 (or_2_out, and_1_out, and_2_out, and_3_out, and_4_out);
  LED L1 (.in(or_2_out));
endmodule
